// Logisim project C.03 - C.04 - C.05 - C.06.circ as structural Verilog: 10 circuits, main circuit C.04 - BCD a 7 SEG
module C_04___BCD_a_7_SEG (
  input  N3,
  input  N2,
  input  N1,
  input  N0
);

  wire a_1_out_5, b_1_out_5, c_1_out_5, d_1_out_5, e_1_out_5, f_1_out_5, g_1_out_5;

  g g_1 (.out_5(g_1_out_5), .a(N3), .b(N2), .c(N1), .d(N0));
  f f_1 (.out_5(f_1_out_5), .a(N3), .b(N2), .c(N1), .d(N0));
  e e_1 (.out_5(e_1_out_5), .a(N3), .b(N2), .c(N1), .d(N0));
  _7_Segment_Display u_7_segment_display_1 (
    .g(g_1_out_5), .f(f_1_out_5), .a(a_1_out_5), .b(b_1_out_5), .e(e_1_out_5), .d(d_1_out_5), .c(c_1_out_5));  // open: dp
  d d_1 (.out_5(d_1_out_5), .a(N3), .b(N2), .c(N1), .d(N0));
  c c_1 (.out_5(c_1_out_5), .a(N3), .b(N2), .c(N1), .d(N0));
  b b_1 (.out_5(b_1_out_5), .a(N3), .b(N2), .c(N1), .d(N0));
  a a_1 (.out_5(a_1_out_5), .a(N3), .b(N2), .c(N1), .d(N0));
endmodule

module g (
  input  a,
  input  b,
  input  c,
  input  d,
  output out_5
);

  wire not_1_out, not_2_out, not_3_out, not_4_out, or_1_out, or_2_out, or_3_out;

  not not_1 (not_1_out, a);
  not not_2 (not_2_out, c);
  not not_3 (not_3_out, b);
  not not_4 (not_4_out, d);
  or or_1 (or_1_out, c, b, a);
  or or_2 (or_2_out, not_4_out, not_2_out, not_3_out, a);
  or or_3 (or_3_out, d, c, not_3_out, not_1_out);
  and and_1 (out_5, or_1_out, or_2_out, or_3_out);
endmodule

module f (
  input  a,
  input  b,
  input  c,
  input  d,
  output out_5
);

  wire not_1_out, not_2_out, not_3_out, not_4_out, or_1_out, or_2_out, or_3_out, or_4_out;

  not not_1 (not_1_out, a);
  not not_2 (not_2_out, b);
  not not_3 (not_3_out, c);
  not not_4 (not_4_out, d);
  or or_1 (or_1_out, not_4_out, b, a);
  or or_2 (or_2_out, not_3_out, b, a);
  or or_3 (or_3_out, not_4_out, not_3_out, a);
  or or_4 (or_4_out, not_4_out, c, not_2_out, not_1_out);
  and and_1 (out_5, or_1_out, or_2_out, or_3_out, or_4_out);
endmodule

module e (
  input  a,
  input  b,
  input  c,
  input  d,
  output out_5
);

  wire not_1_out, not_2_out, or_1_out, or_2_out, or_3_out;

  not not_1 (not_1_out, b);
  not not_2 (not_2_out, d);
  or or_1 (or_1_out, c, not_1_out, a);
  or or_2 (or_2_out, not_2_out, c, b);
  or or_3 (or_3_out, not_2_out, a);
  and and_1 (out_5, or_1_out, or_2_out, or_3_out);
endmodule

module d (
  input  a,
  input  b,
  input  c,
  input  d,
  output out_5
);

  wire not_1_out, not_2_out, not_3_out, not_4_out, or_1_out, or_2_out, or_3_out, or_4_out;

  not not_1 (not_1_out, a);
  not not_2 (not_2_out, c);
  not not_3 (not_3_out, b);
  not not_4 (not_4_out, d);
  or or_1 (or_1_out, d, c, not_3_out, a);
  or or_2 (or_2_out, not_4_out, c, b, a);
  or or_3 (or_3_out, not_1_out, b, not_2_out, d);
  or or_4 (or_4_out, not_4_out, not_2_out, not_3_out);
  and and_1 (out_5, or_1_out, or_2_out, or_3_out, or_4_out);
endmodule

module c (
  input  a,
  input  b,
  input  c,
  input  d,
  output out_5
);

  wire not_1_out, not_2_out, not_3_out, or_1_out, or_2_out, or_3_out;

  not not_1 (not_1_out, a);
  not not_2 (not_2_out, b);
  not not_3 (not_3_out, c);
  or or_1 (or_1_out, d, a, b, not_3_out);
  or or_2 (or_2_out, d, not_2_out, not_1_out);
  or or_3 (or_3_out, not_3_out, not_2_out, not_1_out);
  and and_1 (out_5, or_1_out, or_2_out, or_3_out);
endmodule

module b (
  input  a,
  input  b,
  input  c,
  input  d,
  output out_5
);

  wire not_1_out, not_2_out, not_3_out, not_4_out, or_1_out, or_2_out, or_3_out, or_4_out;

  not not_1 (not_1_out, a);
  not not_2 (not_2_out, b);
  not not_3 (not_3_out, c);
  not not_4 (not_4_out, d);
  or or_1 (or_1_out, not_2_out, not_3_out, d);
  or or_2 (or_2_out, not_1_out, not_2_out, d);
  or or_3 (or_3_out, not_1_out, not_3_out, not_4_out);
  or or_4 (or_4_out, not_4_out, c, not_2_out, a);
  and and_1 (out_5, or_1_out, or_2_out, or_3_out, or_4_out);
endmodule

module a (
  input  a,
  input  b,
  input  c,
  input  d,
  output out_5
);

  wire not_1_out, not_2_out, not_3_out, or_1_out, or_2_out, or_3_out;

  not not_1 (not_1_out, a);
  not not_2 (not_2_out, b);
  not not_3 (not_3_out, d);
  or or_1 (or_1_out, d, c, not_2_out, a);
  or or_2 (or_2_out, not_3_out, c, b, a);
  or or_3 (or_3_out, not_3_out, c, not_2_out, not_1_out);
  and and_1 (out_5, or_1_out, or_2_out, or_3_out);
endmodule

module C_05___Codificador_Simple_16_Entradas (
  input  _0,
  input  _1,
  input  _2,
  input  _3,
  input  _4,
  input  _5,
  input  _6,
  input  _7,
  input  _8,
  input  _9,
  input  A,
  input  B,
  input  C,
  input  D,
  input  E,
  input  F,
  output S0,
  output S1,
  output S2,
  output S3
);

  or or_1 (S0, F, D, B, _9, _7, _5, _3, _1);
  or or_2 (S1, _2, _3, _6, _7, A, B, E, F);
  or or_3 (S2, F, E, D, C, _7, _6, _5, _4);
  or or_4 (S3, F, E, D, C, B, A, _9, _8);
endmodule

module C_06 (
  input  in_1,
  input  in_2,
  input  in_3,
  input  in_4,
  input  in_5,
  input  in_6,
  input  in_7,
  input  in_8,
  input  in_9,
  input  in_10,
  input  in_11,
  input  in_12,
  input  in_13,
  input  in_14,
  input  in_15,
  input  in_16,
  output NADA
);

  wire a_1_out_5, and_1_out, and_2_out, and_3_out, and_4_out, and_5_out, and_6_out, and_7_out, b_1_out_5,
       c_1_out_5, c_05_codificador_simple_16_entradas_1_s0, c_05_codificador_simple_16_entradas_1_s1,
       c_05_codificador_simple_16_entradas_1_s2, c_05_codificador_simple_16_entradas_1_s3, d_1_out_5,
       e_1_out_5, f_1_out_5, g_1_out_5, not_1_out;

  C_05___Codificador_Simple_16_Entradas c_05_codificador_simple_16_entradas_1 (
    .S0(c_05_codificador_simple_16_entradas_1_s0), .S1(c_05_codificador_simple_16_entradas_1_s1),
    .S2(c_05_codificador_simple_16_entradas_1_s2), .S3(c_05_codificador_simple_16_entradas_1_s3), ._0(in_1),
    ._1(in_2), ._2(in_3), ._3(in_4), ._4(in_5), ._5(in_6), ._6(in_7), ._7(in_8), ._8(in_9), ._9(in_10),
    .A(in_11), .B(in_12), .C(in_13), .D(in_14), .E(in_15), .F(in_16));
  nor nor_1 (NADA, in_1, in_2, in_3, in_4, in_5, in_6, in_7, in_8, in_9, in_10, in_11, in_12, in_13, in_14, in_15, in_16);
  not not_1 (not_1_out, NADA);
  g g_1 (
    .out_5(g_1_out_5), .a(c_05_codificador_simple_16_entradas_1_s3),
    .b(c_05_codificador_simple_16_entradas_1_s2), .c(c_05_codificador_simple_16_entradas_1_s1),
    .d(c_05_codificador_simple_16_entradas_1_s0));
  f f_1 (
    .out_5(f_1_out_5), .a(c_05_codificador_simple_16_entradas_1_s3),
    .b(c_05_codificador_simple_16_entradas_1_s2), .c(c_05_codificador_simple_16_entradas_1_s1),
    .d(c_05_codificador_simple_16_entradas_1_s0));
  e e_1 (
    .out_5(e_1_out_5), .a(c_05_codificador_simple_16_entradas_1_s3),
    .b(c_05_codificador_simple_16_entradas_1_s2), .c(c_05_codificador_simple_16_entradas_1_s1),
    .d(c_05_codificador_simple_16_entradas_1_s0));
  d d_1 (
    .out_5(d_1_out_5), .a(c_05_codificador_simple_16_entradas_1_s3),
    .b(c_05_codificador_simple_16_entradas_1_s2), .c(c_05_codificador_simple_16_entradas_1_s1),
    .d(c_05_codificador_simple_16_entradas_1_s0));
  c c_1 (
    .out_5(c_1_out_5), .a(c_05_codificador_simple_16_entradas_1_s3),
    .b(c_05_codificador_simple_16_entradas_1_s2), .c(c_05_codificador_simple_16_entradas_1_s1),
    .d(c_05_codificador_simple_16_entradas_1_s0));
  b b_1 (
    .out_5(b_1_out_5), .a(c_05_codificador_simple_16_entradas_1_s3),
    .b(c_05_codificador_simple_16_entradas_1_s2), .c(c_05_codificador_simple_16_entradas_1_s1),
    .d(c_05_codificador_simple_16_entradas_1_s0));
  a a_1 (
    .out_5(a_1_out_5), .a(c_05_codificador_simple_16_entradas_1_s3),
    .b(c_05_codificador_simple_16_entradas_1_s2), .c(c_05_codificador_simple_16_entradas_1_s1),
    .d(c_05_codificador_simple_16_entradas_1_s0));
  and and_1 (and_1_out, g_1_out_5, not_1_out);
  and and_2 (and_2_out, f_1_out_5, not_1_out);
  and and_3 (and_3_out, e_1_out_5, not_1_out);
  and and_4 (and_4_out, d_1_out_5, not_1_out);
  and and_5 (and_5_out, c_1_out_5, not_1_out);
  and and_6 (and_6_out, b_1_out_5, not_1_out);
  and and_7 (and_7_out, a_1_out_5, not_1_out);
  _7_Segment_Display u_7_segment_display_1 (
    .g(and_1_out), .f(and_2_out), .a(and_7_out), .b(and_6_out), .e(and_3_out), .d(and_4_out), .c(and_5_out));  // open: dp
endmodule
