// Logisim project C.08 - C.09.circ as structural Verilog: 4 circuits, main circuit C.08 - Sumador 4 bits
module C_08___Sumador_4_bits (
  input  A3,
  input  A2,
  input  A1,
  input  A0,
  input  B3,
  input  B2,
  input  B1,
  input  B0,
  output S4,
  output S3,
  output S2,
  output S1,
  output S0
);

  wire full_adder_1_c_out, full_adder_2_c_out, half_adder_1_c;

  Half_Adder half_adder_1 (.A(A0), .B(B0), .S(S0), .C(half_adder_1_c));
  Full_Adder full_adder_1 (.A(A1), .B(B1), .C_In(half_adder_1_c), .S(S1), .C_Out(full_adder_1_c_out));
  Full_Adder full_adder_2 (.A(A2), .B(B2), .C_In(full_adder_1_c_out), .S(S2), .C_Out(full_adder_2_c_out));
  Full_Adder full_adder_3 (.A(A3), .B(B3), .C_In(full_adder_2_c_out), .S(S3), .C_Out(S4));

  // Notes on the sheet:
  //   C Out
  //   C In
  //   C Out
  //   C In
  //   C Out
  //   C Out
  //   C In
endmodule

module Half_Adder (
  input  A,
  input  B,
  output S,
  output C
);

  xor xor_1 (S, A, B);
  and and_1 (C, A, B);
endmodule

module Full_Adder (
  input  A,
  input  B,
  input  C_In,
  output S,
  output C_Out
);

  wire and_1_out, and_2_out, and_3_out, xor_1_out;

  xor xor_1 (xor_1_out, A, B);
  and and_1 (and_1_out, A, B);
  and and_2 (and_2_out, A, C_In);
  and and_3 (and_3_out, B, C_In);
  xor xor_2 (S, xor_1_out, C_In);
  or or_1 (C_Out, and_1_out, and_2_out, and_3_out);
endmodule

module C_09___Sumardor_4_bits_BCD_8421 (
  input  A3,
  input  A2,
  input  A1,
  input  A0,
  input  B3,
  input  B2,
  input  B1,
  input  B0,
  output D3,
  output D2,
  output D1,
  output D0,
  output C3,
  output C2,
  output C1,
  output C0
);

  wire and_1_out, and_2_out, full_adder_1_c_out, full_adder_1_s, full_adder_2_c_out, full_adder_2_s,
       full_adder_3_c_out, full_adder_3_s, full_adder_4_c_out, full_adder_5_c_out, half_adder_1_c,
       half_adder_1_s, half_adder_2_c, or_1_out;

  Half_Adder half_adder_1 (.A(A0), .B(B0), .S(half_adder_1_s), .C(half_adder_1_c));
  Full_Adder full_adder_1 (.A(A1), .B(B1), .C_In(half_adder_1_c), .S(full_adder_1_s), .C_Out(full_adder_1_c_out));
  Full_Adder full_adder_2 (.A(A2), .B(B2), .C_In(full_adder_1_c_out), .S(full_adder_2_s), .C_Out(full_adder_2_c_out));
  Full_Adder full_adder_3 (.A(A3), .B(B3), .C_In(full_adder_2_c_out), .S(full_adder_3_s), .C_Out(full_adder_3_c_out));
  and and_1 (and_1_out, full_adder_2_s, full_adder_3_s);
  and and_2 (and_2_out, full_adder_3_s, full_adder_1_s);
  or or_1 (or_1_out, and_1_out, and_2_out);
  or or_2 (D0, or_1_out, full_adder_3_c_out);
  Half_Adder half_adder_2 (.A(half_adder_1_s), .B(1'b0), .S(C0), .C(half_adder_2_c));
  Full_Adder full_adder_4 (.A(full_adder_1_s), .B(D0), .C_In(half_adder_2_c), .S(C1), .C_Out(full_adder_4_c_out));
  Full_Adder full_adder_5 (.A(full_adder_2_s), .B(D0), .C_In(full_adder_4_c_out), .S(C2), .C_Out(full_adder_5_c_out));
  Full_Adder full_adder_6 (.A(full_adder_3_s), .B(1'b0), .C_In(full_adder_5_c_out), .S(C3));  // open: C_Out

  assign D1 = 1'b0;
  assign D2 = 1'b0;
  assign D3 = 1'b0;

  // Notes on the sheet:
  //   Y0
  //   Y1
  //   Y2
  //   Y3
  //   Carry
  //   A0
  //   B0
  //   A1
  //   B1
  //   A2
  //   B2
  //   A3
  //   B3
endmodule
