// Logisim project C.10.circ as structural Verilog: 1 circuit, main circuit main
module main (
  input  b0,
  input  b1,
  input  b2,
  input  b3,
  input  s1,
  input  s2,
  input  s3,
  output b0_correcto,
  output b1_correcto,
  output b2_correcto,
  output b3_correcto
);

  wire C1_out, C2_out, C3_out, cb0_out, cb1_out, cb2_out, cb3_out, R1_out, R2_out, R3_out;

  ExactlyOne R1 (.out(R1_out), .in0(b0), .in1(b1), .in2(b3));
  ExactlyOne R2 (.out(R2_out), .in0(b0), .in1(b2), .in2(b3));
  ExactlyOne R3 (.out(R3_out), .in0(b1), .in1(b3), .in2(b2));
  xnor C1 (C1_out, R1_out, s1);
  xnor C2 (C2_out, R2_out, s2);
  xnor C3 (C3_out, R3_out, s3);
  and cb0 (cb0_out, ~C1_out, ~C2_out, C3_out);  // AND_Gate
  and cb1 (cb1_out, ~C1_out, C2_out, ~C3_out);  // AND_Gate
  and cb2 (cb2_out, C1_out, ~C2_out, ~C3_out);  // AND_Gate
  and cb3 (cb3_out, ~C1_out, ~C2_out, ~C3_out);  // AND_Gate
  xor xor_1 (b1_correcto, b1, cb1_out);
  xor xor_2 (b2_correcto, cb2_out, b2);
  xor xor_3 (b3_correcto, cb3_out, b3);
  xor xor_4 (b0_correcto, b0, cb0_out);
endmodule
