// Logisim project C.13 - C.14.circ as structural Verilog: 5 circuits, main circuit C.14 - Complemento a la base
module C_14___Complemento_a_la_base (
  input  A3,
  input  A2,
  input  A1,
  input  A0,
  output A3_2,
  output A2_2,
  output A1_2,
  output A0_2
);

  wire full_adder_2_c_out, full_adder_3_c_out, half_adder_1_c, xor_1_out, xor_2_out, xor_3_out, xor_4_out;

  Full_Adder full_adder_1 (.A(xor_2_out), .B(1'b0), .C_In(full_adder_2_c_out), .S(A3_2));  // open: C_Out
  xor xor_1 (xor_1_out, A2, 1'b1);
  xor xor_2 (xor_2_out, A3, 1'b1);
  Full_Adder full_adder_2 (.A(xor_1_out), .B(1'b0), .C_In(full_adder_3_c_out), .S(A2_2), .C_Out(full_adder_2_c_out));
  xor xor_3 (xor_3_out, A1, 1'b1);
  Full_Adder full_adder_3 (.A(xor_3_out), .B(1'b0), .C_In(half_adder_1_c), .S(A1_2), .C_Out(full_adder_3_c_out));
  xor xor_4 (xor_4_out, A0, 1'b1);
  Half_Adder half_adder_1 (.A(xor_4_out), .B(1'b1), .S(A0_2), .C(half_adder_1_c));

  // Notes on the sheet:
  //   B3
  //   A3
  //   S3
  //   B2
  //   A2
  //   S2
  //   A1
  //   S1
  //   B1
  //   Complemento a la base -1
  //   Complemento a la base
endmodule

module Half_Adder (
  input  A,
  input  B,
  output S,
  output C
);

  xor xor_1 (S, A, B);
  and and_1 (C, A, B);
endmodule

module Full_Adder (
  input  A,
  input  B,
  input  C_In,
  output S,
  output C_Out
);

  wire and_1_out, and_2_out, and_3_out, xor_1_out;

  xor xor_1 (xor_1_out, A, B);
  and and_1 (and_1_out, A, B);
  and and_2 (and_2_out, A, C_In);
  and and_3 (and_3_out, B, C_In);
  xor xor_2 (S, xor_1_out, C_In);
  or or_1 (C_Out, and_1_out, and_2_out, and_3_out);
endmodule

module Sumador_4_bits (
  input  in_1,
  input  in_2,
  input  in_3,
  input  in_4,
  input  in_5,
  input  in_6,
  input  in_7,
  input  in_8,
  output out_9,
  output out_10,
  output out_11,
  output out_12,
  output out_13
);

  wire full_adder_2_c_out, full_adder_3_c_out, half_adder_1_c;

  Full_Adder full_adder_1 (.A(in_1), .B(in_5), .C_In(full_adder_2_c_out), .S(out_10), .C_Out(out_9));
  Full_Adder full_adder_2 (.A(in_2), .B(in_6), .C_In(full_adder_3_c_out), .S(out_11), .C_Out(full_adder_2_c_out));
  Full_Adder full_adder_3 (.A(in_3), .B(in_7), .C_In(half_adder_1_c), .S(out_12), .C_Out(full_adder_3_c_out));
  Half_Adder half_adder_1 (.A(in_4), .B(in_8), .S(out_13), .C(half_adder_1_c));

  // Notes on the sheet:
  //   A3
  //   B3
  //   S3
  //   A2
  //   B2
  //   S2
  //   B1
  //   A1
  //   S1
endmodule

module C_13___Restador_4_Bits (
  input  B3,
  input  B2,
  input  B1,
  input  B0,
  input  A3,
  input  A2,
  input  A1,
  input  A0,
  output A__B,
  output A_B,
  output out_11,
  output out_12,
  output out_13,
  output out_14,
  output A__B_2,
  output Borrow,
  output A__B_3,
  output A_B_2,
  output A_B_3
);

  wire c_14_complemento_a_la_base_1_a0_2, c_14_complemento_a_la_base_1_a1_2,
       c_14_complemento_a_la_base_1_a2_2, c_14_complemento_a_la_base_1_a3_2;

  C_14___Complemento_a_la_base c_14_complemento_a_la_base_1 (
    .A3(B3), .A2(B2), .A1(B1), .A0(B0), .A3_2(c_14_complemento_a_la_base_1_a3_2),
    .A2_2(c_14_complemento_a_la_base_1_a2_2), .A1_2(c_14_complemento_a_la_base_1_a1_2),
    .A0_2(c_14_complemento_a_la_base_1_a0_2));
  Sumador_4_bits sumador_4_bits_1 (
    .in_1(A3), .in_2(A2), .in_3(A1), .in_4(A0), .in_5(c_14_complemento_a_la_base_1_a3_2),
    .in_6(c_14_complemento_a_la_base_1_a2_2), .in_7(c_14_complemento_a_la_base_1_a1_2),
    .in_8(c_14_complemento_a_la_base_1_a0_2), .out_9(A_B_3), .out_10(out_11), .out_11(out_12),
    .out_12(out_13), .out_13(out_14));
  not not_1 (A_B_2, A_B_3);
  nor nor_1 (A_B, out_14, out_13, out_12, out_11);
  not not_2 (A__B, A_B);
  or or_1 (A__B_2, A_B, A_B_2);
  or or_2 (A__B_3, A_B, A_B_3);

  assign Borrow = A_B_2;

  // Notes on the sheet:
  //   Complemento a la base
endmodule
