// Logisim project Ejercicios Guia 0.4 - Circuitos Secuenciales.circ as structural Verilog
module Flip_Flop_RS_Asincronico (
  input  R,
  input  S,
  output Q,
  output nQ
);

  nor A (Q, R, nQ);
  nor B (nQ, Q, S);
endmodule

module Flip_Flor_RS_Asincronico_con_NAND (
  input  S,
  input  R,
  output Q,
  output nQ
);

  nand nand_1 (Q, S, nQ);
  nand nand_2 (nQ, Q, R);
endmodule

module Flip_Flop_RS_Sincronico (
  input  R,
  input  E,
  input  S,
  output Q,
  output nQ
);

  wire and_1_out, and_2_out;

  and and_1 (and_1_out, R, E);
  and and_2 (and_2_out, E, S);
  nor A (Q, and_1_out, nQ);
  nor B (nQ, Q, and_2_out);
endmodule

module Flip_Flop_D_por_Nivel (
  input  D,
  input  E,
  output Q,
  output nQ
);

  wire and_1_out, and_2_out, not_1_out;

  not not_1 (not_1_out, D);
  and and_1 (and_1_out, not_1_out, E);
  and and_2 (and_2_out, E, D);
  nor A (Q, and_1_out, nQ);
  nor B (nQ, Q, and_2_out);
endmodule

module Detector_de_Flancos (
  input  Clock,
  output Flanco
);

  wire not_1_out, not_2_out, not_3_out;

  not not_1 (not_1_out, Clock);
  not not_2 (not_2_out, not_1_out);
  not not_3 (not_3_out, not_2_out);
  and and_1 (Flanco, Clock, not_3_out);

  // Notes on the sheet:
  //   Delay
endmodule

module Flip_Flop_D_por_Flanco_Ascendente (
  input  D,
  input  Clock,
  output Q
);

  wire and_1_out, and_2_out, and_3_out, nor_2_out, not_1_out, not_2_out, not_3_out, not_4_out;

  not not_1 (not_1_out, Clock);
  not not_2 (not_2_out, not_1_out);
  not not_3 (not_3_out, not_2_out);
  and and_1 (and_1_out, Clock, not_3_out);
  not not_4 (not_4_out, D);
  and and_2 (and_2_out, not_4_out, and_1_out);
  and and_3 (and_3_out, and_1_out, D);
  nor nor_1 (Q, and_2_out, nor_2_out);
  nor nor_2 (nor_2_out, Q, and_3_out);
endmodule

module Flip_Flop_D_por_Flanco_Descendente (
  input  D,
  input  Clock,
  output Q,
  output nQ
);

  wire and_1_out, and_2_out, and_3_out, not_1_out, not_2_out, not_3_out, not_4_out, not_5_out;

  not not_1 (not_1_out, Clock);
  not not_2 (not_2_out, not_1_out);
  not not_3 (not_3_out, not_2_out);
  and and_1 (and_1_out, Clock, not_3_out);
  not not_4 (not_4_out, D);
  not not_5 (not_5_out, and_1_out);
  and and_2 (and_2_out, not_4_out, not_5_out);
  and and_3 (and_3_out, not_5_out, D);
  nor A (Q, and_2_out, nQ);
  nor B (nQ, Q, and_3_out);
endmodule

module Flip_Flop_D_por_Flanco_Ascendente_con_Clear_Sincronico (
  input  nCLR,
  input  D,
  input  Clock,
  output Q,
  output nQ
);

  wire and_1_out, and_2_out, and_3_out, and_4_out, not_1_out, not_2_out, not_3_out, not_4_out;

  not not_1 (not_1_out, Clock);
  not not_2 (not_2_out, not_1_out);
  not not_3 (not_3_out, not_2_out);
  and and_1 (and_1_out, nCLR, D);
  and and_2 (and_2_out, Clock, not_3_out);
  not not_4 (not_4_out, and_1_out);
  and and_3 (and_3_out, not_4_out, and_2_out);
  and and_4 (and_4_out, and_2_out, and_1_out);
  nor A (Q, and_3_out, nQ);
  nor B (nQ, Q, and_4_out);
endmodule

module Flip_Flop_D_por_Flanco_Descendente_con_Clear_Sincronico (
  input  nCLR,
  input  D,
  input  Clock,
  output Q,
  output nQ
);

  wire and_1_out, and_2_out, and_3_out, and_4_out, not_1_out, not_2_out, not_3_out, not_4_out, not_5_out;

  not not_1 (not_1_out, Clock);
  not not_2 (not_2_out, not_1_out);
  not not_3 (not_3_out, not_2_out);
  and and_1 (and_1_out, nCLR, D);
  and and_2 (and_2_out, Clock, not_3_out);
  not not_4 (not_4_out, and_1_out);
  not not_5 (not_5_out, and_2_out);
  and and_3 (and_3_out, not_4_out, not_5_out);
  and and_4 (and_4_out, not_5_out, and_1_out);
  nor A (Q, and_3_out, nQ);
  nor B (nQ, Q, and_4_out);
endmodule

module Flip_Flop_T_por_Flanco_Ascendente_con_Clear_Sincronico (
  input  nCLR,
  input  T,
  input  Clock,
  output Q
);

  wire and_1_out, and_2_out, and_3_out, and_4_out, nor_2_out, not_1_out, not_2_out, not_3_out, not_4_out,
       xor_1_out;

  xor xor_1 (xor_1_out, Q, T);
  not not_1 (not_1_out, not_2_out);
  not not_2 (not_2_out, Clock);
  not not_3 (not_3_out, not_1_out);
  and and_1 (and_1_out, nCLR, xor_1_out);
  and and_2 (and_2_out, Clock, not_3_out);
  not not_4 (not_4_out, and_1_out);
  and and_3 (and_3_out, not_4_out, and_2_out);
  and and_4 (and_4_out, and_2_out, and_1_out);
  nor nor_1 (Q, and_3_out, nor_2_out);
  nor nor_2 (nor_2_out, Q, and_4_out);
endmodule

module Flip_Flop_RS_Sincronico_con_NAND (
  input  S,
  input  E,
  input  R,
  output Q,
  output nQ
);

  wire nand_1_out, nand_2_out;

  nand nand_1 (nand_1_out, S, E);
  nand nand_2 (nand_2_out, E, R);
  nand nand_3 (Q, nand_1_out, nQ);
  nand nand_4 (nQ, Q, nand_2_out);
endmodule

module Flip_Flor_D_por_Nivel_con_NAND (
  input  D,
  input  E,
  output Q,
  output nQ
);

  wire and_1_out, and_2_out, not_1_out;

  not not_1 (not_1_out, D);
  and and_1 (and_1_out, not_1_out, E);
  and and_2 (and_2_out, E, D);
  nand nand_1 (Q, and_1_out, nQ);
  nand nand_2 (nQ, Q, and_2_out);
endmodule

module D_04___Registro_de_desplazamiento_4_bits (
  input  In,
  input  Clock,
  input  NoLeft,
  output S3,
  output S2,
  output S1,
  output S0
);

  wire multiplexer_1_out, multiplexer_2_out, multiplexer_3_out, multiplexer_4_out;

  Multiplexer #(.enable("false")) multiplexer_1 (.in0(S2), .in1(In), .out(multiplexer_1_out), .sel(NoLeft));
  Flip_Flop_D_por_Flanco_Ascendente flip_flop_d_por_flanco_ascendente_1 (.D(multiplexer_1_out), .Q(S3), .Clock(Clock));
  Multiplexer #(.enable("false")) multiplexer_2 (.in0(S1), .in1(S3), .out(multiplexer_2_out), .sel(NoLeft));
  Flip_Flop_D_por_Flanco_Ascendente flip_flop_d_por_flanco_ascendente_2 (.D(multiplexer_2_out), .Q(S2), .Clock(Clock));
  Multiplexer #(.enable("false")) multiplexer_3 (.in0(S0), .in1(S2), .out(multiplexer_3_out), .sel(NoLeft));
  Flip_Flop_D_por_Flanco_Ascendente flip_flop_d_por_flanco_ascendente_3 (.D(multiplexer_3_out), .Q(S1), .Clock(Clock));
  Multiplexer #(.enable("false")) multiplexer_4 (.in0(In), .in1(S1), .out(multiplexer_4_out), .sel(NoLeft));
  Flip_Flop_D_por_Flanco_Ascendente flip_flop_d_por_flanco_ascendente_4 (.D(multiplexer_4_out), .Q(S0), .Clock(Clock));
endmodule

module Latch_4_bits (
  input  A0,
  input  A1,
  input  A2,
  input  A3,
  input  Clock,
  output B0,
  output B1,
  output B2,
  output B3
);

  Flip_Flop_D_por_Flanco_Ascendente flip_flop_d_por_flanco_ascendente_1 (.D(A0), .Q(B0), .Clock(Clock));
  Flip_Flop_D_por_Flanco_Ascendente flip_flop_d_por_flanco_ascendente_2 (.D(A1), .Q(B1), .Clock(Clock));
  Flip_Flop_D_por_Flanco_Ascendente flip_flop_d_por_flanco_ascendente_3 (.D(A2), .Q(B2), .Clock(Clock));
  Flip_Flop_D_por_Flanco_Ascendente flip_flop_d_por_flanco_ascendente_4 (.D(A3), .Q(B3), .Clock(Clock));
endmodule

module Shift_Right_4_Bits (
  input  In,
  input  Clock,
  output B0,
  output B1,
  output B2,
  output B3
);

  Flip_Flop_D_por_Flanco_Ascendente flip_flop_d_por_flanco_ascendente_1 (.D(In), .Q(B0), .Clock(Clock));
  Flip_Flop_D_por_Flanco_Ascendente flip_flop_d_por_flanco_ascendente_2 (.D(B0), .Q(B1), .Clock(Clock));
  Flip_Flop_D_por_Flanco_Ascendente flip_flop_d_por_flanco_ascendente_3 (.D(B1), .Q(B2), .Clock(Clock));
  Flip_Flop_D_por_Flanco_Ascendente flip_flop_d_por_flanco_ascendente_4 (.D(B2), .Q(B3), .Clock(Clock));
endmodule

module Flip_Flop_T_por_Flanco_Ascendente__No_funciona (
  input  T,
  input  Clock,
  output Q
);

  wire and_1_out, and_2_out, and_3_out, nor_2_out, not_1_out, not_2_out, not_3_out, not_4_out, xor_1_out;

  not not_1 (not_1_out, not_2_out);
  not not_2 (not_2_out, Clock);
  not not_3 (not_3_out, not_1_out);
  xor xor_1 (xor_1_out, Q, T);
  and and_1 (and_1_out, Clock, not_3_out);
  not not_4 (not_4_out, xor_1_out);
  and and_2 (and_2_out, not_4_out, and_1_out);
  and and_3 (and_3_out, and_1_out, xor_1_out);
  nor nor_1 (Q, and_2_out, nor_2_out);
  nor nor_2 (nor_2_out, Q, and_3_out);
endmodule

module Contador_Sincronico_Modulo_5 (
  input  Clock,
  input  En
);

  wire and_1_out, and_2_out, flip_flop_t_por_flanco_ascendente_con_clear_sincronico_1_q,
       flip_flop_t_por_flanco_ascendente_con_clear_sincronico_2_q,
       flip_flop_t_por_flanco_ascendente_con_clear_sincronico_3_q, nand_1_out;

  and and_1 (and_1_out, Clock, En);
  nand nand_1 (nand_1_out, flip_flop_t_por_flanco_ascendente_con_clear_sincronico_1_q, flip_flop_t_por_flanco_ascendente_con_clear_sincronico_3_q);
  Flip_Flop_T_por_Flanco_Ascendente_con_Clear_Sincronico flip_flop_t_por_flanco_ascendente_con_clear_sincronico_1 (
    .nCLR(1'b1), .T(and_1_out), .Clock(nand_1_out),
    .Q(flip_flop_t_por_flanco_ascendente_con_clear_sincronico_1_q));
  Flip_Flop_T_por_Flanco_Ascendente_con_Clear_Sincronico flip_flop_t_por_flanco_ascendente_con_clear_sincronico_2 (
    .nCLR(flip_flop_t_por_flanco_ascendente_con_clear_sincronico_1_q), .T(and_1_out), .Clock(nand_1_out),
    .Q(flip_flop_t_por_flanco_ascendente_con_clear_sincronico_2_q));
  and and_2 (and_2_out, flip_flop_t_por_flanco_ascendente_con_clear_sincronico_1_q, flip_flop_t_por_flanco_ascendente_con_clear_sincronico_2_q);
  Flip_Flop_T_por_Flanco_Ascendente_con_Clear_Sincronico flip_flop_t_por_flanco_ascendente_con_clear_sincronico_3 (
    .nCLR(and_2_out), .T(and_1_out), .Clock(nand_1_out),
    .Q(flip_flop_t_por_flanco_ascendente_con_clear_sincronico_3_q));
endmodule

module Flip_Flop_T_por_Flanco_Descencente_con_Clear_Sincronico (
  input  nCLR,
  input  T,
  input  Clock,
  output Q
);

  wire and_1_out, and_2_out, and_3_out, and_4_out, nor_2_out, not_1_out, not_2_out, not_3_out, not_4_out,
       not_5_out, xor_1_out;

  xor xor_1 (xor_1_out, Q, T);
  not not_1 (not_1_out, Clock);
  not not_2 (not_2_out, not_1_out);
  not not_3 (not_3_out, not_2_out);
  and and_1 (and_1_out, nCLR, xor_1_out);
  not not_4 (not_4_out, and_2_out);
  and and_2 (and_2_out, Clock, not_3_out);
  not not_5 (not_5_out, and_1_out);
  and and_3 (and_3_out, not_5_out, not_4_out);
  and and_4 (and_4_out, not_4_out, and_1_out);
  nor nor_1 (Q, and_3_out, nor_2_out);
  nor nor_2 (nor_2_out, Q, and_4_out);
endmodule

module Contador_Sincronico_Modulo_N_Anillo (
  input  Clock,
  output Q0,
  output Q1,
  output Q2
);

  wire nor_1_out, or_1_out;

  nor nor_1 (nor_1_out, Q2, Q1, Q0);
  or or_1 (or_1_out, nor_1_out, Q2);
  Flip_Flop_D_por_Flanco_Ascendente flip_flop_d_por_flanco_ascendente_1 (.D(or_1_out), .Q(Q0), .Clock(Clock));
  Flip_Flop_D_por_Flanco_Ascendente flip_flop_d_por_flanco_ascendente_2 (.D(Q0), .Q(Q1), .Clock(Clock));
  Flip_Flop_D_por_Flanco_Ascendente flip_flop_d_por_flanco_ascendente_3 (.D(Q1), .Q(Q2), .Clock(Clock));
endmodule
